# Fritzing sketch jiin_Bluetooth (saved by Fritzing 0.9.3b)

parts:
  부품1 = Arduino Uno (Rev3)
  부품2 = Bluetooth HC-05 Macho

nets:
  N1: 부품1.D2, 부품2.RXD
  N2: 부품1.D3_PWM, 부품2.TXD
  5V: 부품1.5V, 부품2.VCC
  GND: 부품1.GND, 부품2.GND

notes:
  블루투스 모듈 HC-06이 존재하지 않아
  다른 블루투스 모듈인 HC-05로 공부 진행했습니다.
  [참고]
  https://bugwhale.com/bluetooth-communication-module-01/

// code stored in the sketch: jiin_Bluetooth.code.ino
#include <SoftwareSerial.h>

//? ?? ??
#define PIN_TX 3
#define PIN_RX 2

//????? ??? ?? ??
SoftwareSerial btSerial(PIN_TX, PIN_RX);

void setup()
{
	Serial.begin(9600);
	btSerial.begin(9600);
}

void loop()
{
	if(Serial.available()){
		btSerial.write(Serial.read());
	}
	if(btSerial.available()){
		Serial.write(btSerial.read());
	}
}
